// Logisim project project.circ as structural Verilog: 11 circuits, main circuit main
module main (
  input  in_1,
  input  [31:0] in_2,
  input  [31:0] in_3,
  input  in_4,
  input  in_5,
  output [31:0] out_6,
  output [31:0] out_7,
  output [31:0] out_8,
  output [31:0] out_9,
  output [31:0] out_10,
  output [31:0] out_11
);

  wire clock_1_out;

  Clock clock_1 (.out(clock_1_out));
  connected connected_1 (
    .clk(clock_1_out), .reset(in_1), .in_add(in_2), .y_input(in_3), .first_en_this(in_4), .sec_en_this(in_5),
    .instruction(out_6), .pc_now(out_7), .out_28(out_8), .out_29(out_9), .out_30(out_10), .out_31(out_11));
endmodule

module RegFile (
  input  [31:0] instru_in,
  input  [31:0] rd,
  input  we,
  input  clk,
  input  reset,
  output [31:0] rs1,
  output [31:0] rs2,
  output [31:0] out_28,
  output [31:0] out_29,
  output [31:0] Out_30,
  output [31:0] Out_31
);

  wire x0we, x1we, x2we, x3we, x4we, x5we, x6we, x7we, x8we, x9we, x10we, x11we, x12we, x13we, x14we, x15we,
       x16we, x17we, x18we, x19we, x20we, x21we, x22we, x23we, x24we, x25we, x26we, x27we, x28we, x29we,
       x30we, x31we;
  wire [31:0] x0q, x1q, x2q, x3q, x4q, x5q, x6q, x7q, x8q, x9q, x10q, x11q, x12q, x13q, x14q, x15q, x16q,
       x17q, x18q, x19q, x20q, x21q, x22q, x23q, x24q, x25q, x26q, x27q;

  Demultiplexer #(.select(5)) demultiplexer_1 (
    .out0(x0we), .out1(x1we), .out2(x2we), .out3(x3we), .out4(x4we), .out5(x5we), .out6(x6we), .out7(x7we),
    .out8(x8we), .out9(x9we), .out10(x10we), .out11(x11we), .out12(x12we), .out13(x13we), .out14(x14we),
    .out15(x15we), .out16(x16we), .out17(x17we), .out18(x18we), .out19(x19we), .out20(x20we), .out21(x21we),
    .out22(x22we), .out23(x23we), .out24(x24we), .out25(x25we), .out26(x26we), .out27(x27we), .out28(x28we),
    .out29(x29we), .out30(x30we), .out31(x31we), .in(we), .sel(instru_in[11:7]));
  Register #(.width(32)) zerox (.D(rd), .en(1'b0), .clk(clk), .Q(x0q), .clr(reset));
  Register #(.width(32)) fourx (.D(rd), .en(x4we), .clk(clk), .Q(x4q), .clr(reset));
  Register #(.width(32)) eightx (.D(rd), .en(x8we), .clk(clk), .Q(x8q), .clr(reset));
  Register #(.width(32)) twelvex (.D(rd), .en(x12we), .clk(clk), .Q(x12q), .clr(reset));
  Register #(.width(32)) sixteenx (.D(rd), .en(x16we), .clk(clk), .Q(x16q), .clr(reset));
  Register #(.width(32)) twentyx (.D(rd), .en(x20we), .clk(clk), .Q(x20q), .clr(reset));
  Register #(.width(32)) twentyfourx (.D(rd), .en(x24we), .clk(clk), .Q(x24q), .clr(reset));
  Register #(.width(32)) twentyeightx (.D(rd), .en(x28we), .clk(clk), .Q(out_28), .clr(reset));
  Register #(.width(32)) onex (.D(rd), .en(x1we), .clk(clk), .Q(x1q), .clr(reset));
  Register #(.width(32)) fivex (.D(rd), .en(x5we), .clk(clk), .Q(x5q), .clr(reset));
  Register #(.width(32)) ninex (.D(rd), .en(x9we), .clk(clk), .Q(x9q), .clr(reset));
  Register #(.width(32)) thirteenx (.D(rd), .en(x13we), .clk(clk), .Q(x13q), .clr(reset));
  Register #(.width(32)) seventeenx (.D(rd), .en(x17we), .clk(clk), .Q(x17q), .clr(reset));
  Register #(.width(32)) twentyonex (.D(rd), .en(x21we), .clk(clk), .Q(x21q), .clr(reset));
  Register #(.width(32)) twentyfivex (.D(rd), .en(x25we), .clk(clk), .Q(x25q), .clr(reset));
  Register #(.width(32)) twentyninex (.D(rd), .en(x29we), .clk(clk), .Q(out_29), .clr(reset));
  Register #(.width(32)) twox (.D(rd), .en(x2we), .clk(clk), .Q(x2q), .clr(reset));
  Register #(.width(32)) sixx (.D(rd), .en(x6we), .clk(clk), .Q(x6q), .clr(reset));
  Register #(.width(32)) tenx (.D(rd), .en(x10we), .clk(clk), .Q(x10q), .clr(reset));
  Register #(.width(32)) fouteenx (.D(rd), .en(x14we), .clk(clk), .Q(x14q), .clr(reset));
  Register #(.width(32)) eighteenx (.D(rd), .en(x18we), .clk(clk), .Q(x18q), .clr(reset));
  Register #(.width(32)) twentytwox (.D(rd), .en(x22we), .clk(clk), .Q(x22q), .clr(reset));
  Register #(.width(32)) twentysixx (.D(rd), .en(x26we), .clk(clk), .Q(x26q), .clr(reset));
  Register #(.width(32)) thirtyx (.D(rd), .en(x30we), .clk(clk), .Q(Out_30), .clr(reset));
  Register #(.width(32)) threex (.D(rd), .en(x3we), .clk(clk), .Q(x3q), .clr(reset));
  Register #(.width(32)) sevenx (.D(rd), .en(x7we), .clk(clk), .Q(x7q), .clr(reset));
  Register #(.width(32)) elevenx (.D(rd), .en(x11we), .clk(clk), .Q(x11q), .clr(reset));
  Register #(.width(32)) fifteenx (.D(rd), .en(x15we), .clk(clk), .Q(x15q), .clr(reset));
  Register #(.width(32)) ninteenx (.D(rd), .en(x19we), .clk(clk), .Q(x19q), .clr(reset));
  Register #(.width(32)) twentythreex (.D(rd), .en(x23we), .clk(clk), .Q(x23q), .clr(reset));
  Register #(.width(32)) twentysevenx (.D(rd), .en(x27we), .clk(clk), .Q(x27q), .clr(reset));
  Register #(.width(32)) thirtyonex (.D(rd), .en(x31we), .clk(clk), .Q(Out_31), .clr(reset));
  Multiplexer #(.select(5), .width(32)) multiplexer_1 (
    .in0(x0q), .in1(x1q), .in2(x2q), .in3(x3q), .in4(x4q), .in5(x5q), .in6(x6q), .in7(x7q), .in8(x8q),
    .in9(x9q), .in10(x10q), .in11(x11q), .in12(x12q), .in13(x13q), .in14(x14q), .in15(x15q), .in16(x16q),
    .in17(x17q), .in18(x18q), .in19(x19q), .in20(x20q), .in21(x21q), .in22(x22q), .in23(x23q), .in24(x24q),
    .in25(x25q), .in26(x26q), .in27(x27q), .in28(out_28), .in29(out_29), .in30(Out_30), .in31(Out_31),
    .out(rs1), .sel(instru_in[19:15]));
  Multiplexer #(.select(5), .width(32)) multiplexer_2 (
    .in0(x0q), .in1(x1q), .in2(x2q), .in3(x3q), .in4(x4q), .in5(x5q), .in6(x6q), .in7(x7q), .in8(x8q),
    .in9(x9q), .in10(x10q), .in11(x11q), .in12(x12q), .in13(x13q), .in14(x14q), .in15(x15q), .in16(x16q),
    .in17(x17q), .in18(x18q), .in19(x19q), .in20(x20q), .in21(x21q), .in22(x22q), .in23(x23q), .in24(x24q),
    .in25(x25q), .in26(x26q), .in27(x27q), .in28(out_28), .in29(out_29), .in30(Out_30), .in31(Out_31),
    .out(rs2), .sel(instru_in[24:20]));

  // Other names for the same wires on the sheet: clk_t = clk; rdi_t[4:0] = instru_in[11:7];
  //   rsi1_t[4:0] = instru_in[19:15]; rsi2_t[4:0] = instru_in[24:20]; rd_t[31:0] = rd; rs1_t[31:0] = rs1;
  //   rs2_t[31:0] = rs2; rse = reset; we_t = we; x28q[31:0] = out_28; x29q[31:0] = out_29; x30q[31:0] = Out_30;
  //   x31q[31:0] = Out_31
endmodule

module ALU (
  input  [31:0] dataA,
  input  [31:0] dataB,
  input  [3:0] sel,
  output lt,
  output ltu,
  output zero,
  output [31:0] dataD
);

  wire comparator_1_lt, comparator_2_lt;
  wire [31:0] addout, andout, orout, sllout, sraout, srlout, subout, xorout;
  wire [31:1] sltout, sltuout;

  Adder #(.width(32)) adder_1 (.a(dataA), .b(dataB), .out(addout));  // open: cin, cout
  Subtractor #(.width(32)) subtractor_1 (.a(dataA), .b(dataB), .out(subout));  // open: bin, bout
  Shifter #(.width(32)) shifter_1 (.in(dataA), .\dist (dataB[4:0]), .out(sllout));
  Comparator #(.width(32)) comparator_1 (.a(dataA), .b(dataB), .lt(comparator_1_lt));  // open: gt, eq
  assign {sltout, lt} = {{31{comparator_1_lt}}, comparator_1_lt};  // Bit_Extender bit_extender_1
  Comparator #(.mode("unsigned"), .width(32)) comparator_2 (
    .a(dataA), .b(dataB), .lt(comparator_2_lt));  // open: gt, eq
  assign {sltuout, ltu} = {{31{comparator_2_lt}}, comparator_2_lt};  // Bit_Extender bit_extender_2
  assign xorout = dataA ^ dataB;  // XOR_Gate xor_1, 32 bits wide
  Shifter #(.shift("lr"), .width(32)) shifter_2 (.in(dataA), .\dist (dataB[4:0]), .out(srlout));
  Shifter #(.shift("ar"), .width(32)) shifter_3 (.in(dataA), .\dist (dataB[4:0]), .out(sraout));
  assign orout = dataA | dataB;  // OR_Gate or_1, 32 bits wide
  assign andout = dataA & dataB;  // AND_Gate and_1, 32 bits wide
  Comparator #(.width(32)) comparator_3 (.a(subout), .b({32{1'b0}}), .eq(zero));  // open: gt, lt
  Multiplexer #(.select(4), .width(32)) multiplexer_1 (
    .in0(addout), .in1(sllout), .in2({sltout, lt}), .in3({sltuout, ltu}), .in4(xorout), .in5(srlout),
    .in6(orout), .in7(andout), .in8(subout), .in13(sraout), .out(dataD), .sel(sel));  // open: in9, in10, in11, in12, in14, in15

  // Other names for the same wires on the sheet: dataA_t[31:0] = dataA; dataB50[4:0] = dataB[4:0];
  //   dataB_t[31:0] = dataB; dataD_t[31:0] = dataD; sel_t[3:0] = sel; sltout[0] = lt; sltuout[0] = ltu
endmodule

module immgen (
  input  [1:0] imm_sel,
  input  [31:0] instr,
  output [31:0] imm_out
);

  wire [31:0] bit_extender_1_out, bit_extender_2_out, bit_extender_3_out, bit_extender_4_out;

  assign bit_extender_1_out = {{20{instr[31]}}, {instr[31:25], instr[11:7]}};  // Bit_Extender bit_extender_1
  assign bit_extender_2_out = {{20{instr[31]}}, instr[31:20]};  // Bit_Extender bit_extender_2
  assign bit_extender_3_out = {{19{instr[31]}}, {instr[31], instr[7], instr[30:25], instr[11:8], 1'b0}};  // Bit_Extender bit_extender_3
  assign bit_extender_4_out = {{11{instr[31]}}, {instr[31], instr[19:12], instr[20], instr[30:21], 1'b0}};  // Bit_Extender bit_extender_4
  Multiplexer #(.select(3), .width(32)) multiplexer_1 (
    .in0(bit_extender_2_out), .in1(bit_extender_1_out), .in2(bit_extender_3_out), .in3(bit_extender_4_out),
    .in4({instr[31:12], {12{1'b0}}}), .out(imm_out), .sel({1'b0, imm_sel}));  // open: in5, in6, in7

  // Notes on the sheet:
  //   s_imm
  //   i_imm
  //   b_imm
  //   u_imm
  //   j_imm
endmodule

module instrmem (
  input  [31:0] pc_in,
  output [31:0] instruction_out
);

  ROM #(.addrWidth(10), .dataWidth(32)) rom_1 (.addr(pc_in[11:2]), .data(instruction_out));

  // Notes on the sheet:
  //   contents of rom_1 (hex, n*v repeats v):
  //   1400093 a103 200193 2800313 e93 f13 f93 4314863 200213 100393 2320263 182b3 42c863 404282b3 28863
  //   ff5ff06f 120213 fe5ff06f 393 38c63 332023 430313 1e8e93 f0fb3 18f33 118193 fb5ff06f 6f
endmodule

module pc (
  input  [1:0] pcsrc,
  input  clk,
  input  reset,
  input  [31:0] imm,
  input  [31:0] rs1_data,
  output [31:0] pc_out,
  output [31:0] pcplus4
);

  wire and_1_out, and_2_out, and_3_out, not_1_out, not_2_out;
  wire [31:0] adder_2_out, adder_3_out, multiplexer_1_out, multiplexer_2_out, multiplexer_3_out;

  and and_1 (and_1_out, pcsrc[0], not_1_out);
  not not_1 (not_1_out, pcsrc[1]);
  not not_2 (not_2_out, pcsrc[0]);
  and and_2 (and_2_out, not_2_out, pcsrc[1]);
  and and_3 (and_3_out, pcsrc[0], pcsrc[1]);
  Register #(.width(32)) register_1 (.D(multiplexer_3_out), .en(1'b1), .clk(clk), .Q(pc_out), .clr(reset));
  Adder #(.width(32)) adder_1 (.a(pc_out), .b(32'h4), .out(pcplus4));  // open: cin, cout
  Adder #(.width(32)) adder_2 (.a(pc_out), .b(imm), .out(adder_2_out));  // open: cin, cout
  Adder #(.width(32)) adder_3 (.a(rs1_data), .b(imm), .out(adder_3_out));  // open: cin, cout
  Multiplexer #(.width(32)) multiplexer_1 (.in0(pcplus4), .in1(adder_2_out), .out(multiplexer_1_out), .sel(and_1_out));
  Multiplexer #(.width(32)) multiplexer_2 (
    .in0(multiplexer_1_out), .in1(adder_2_out), .out(multiplexer_2_out), .sel(and_2_out));
  Multiplexer #(.width(32)) multiplexer_3 (
    .in0(multiplexer_2_out), .in1(adder_3_out), .out(multiplexer_3_out), .sel(and_3_out));

  // Other names for the same wires on the sheet: i[31:0] = pcplus4; pc0 = pcsrc[0]; pc1 = pcsrc[1]
endmodule

module controlunit (
  input  take,
  input  [31:0] instu_in,
  output [1:0] pcsrc,
  output [1:0] resultsrc,
  output memwrite,
  output memread,
  output alusrc,
  output [1:0] immsrc,
  output regwrite,
  output [1:0] aluop,
  output branch,
  output R,
  output lor
);

  wire I_t, jal_t, jalr_t, not_1_out, not_2_out, not_3_out, not_4_out, not_5_out, not_6_out, not_7_out,
       not_8_out, not_9_out, not_10_out, not_11_out, not_12_out, not_13_out, not_14_out, not_15_out,
       not_16_out, not_17_out, not_18_out, not_19_out, not_20_out, not_21_out, not_22_out;

  not not_1 (not_1_out, instu_in[2]);
  not not_2 (not_2_out, instu_in[3]);
  not not_3 (not_3_out, instu_in[6]);
  not not_4 (not_4_out, instu_in[2]);
  not not_5 (not_5_out, instu_in[3]);
  not not_6 (not_6_out, instu_in[5]);
  not not_7 (not_7_out, instu_in[6]);
  not not_8 (not_8_out, instu_in[2]);
  not not_9 (not_9_out, instu_in[3]);
  not not_10 (not_10_out, instu_in[4]);
  not not_11 (not_11_out, instu_in[5]);
  not not_12 (not_12_out, instu_in[6]);
  not not_13 (not_13_out, instu_in[2]);
  not not_14 (not_14_out, instu_in[3]);
  not not_15 (not_15_out, instu_in[4]);
  not not_16 (not_16_out, instu_in[6]);
  not not_17 (not_17_out, instu_in[2]);
  not not_18 (not_18_out, instu_in[3]);
  not not_19 (not_19_out, instu_in[4]);
  not not_20 (not_20_out, instu_in[4]);
  not not_21 (not_21_out, instu_in[3]);
  not not_22 (not_22_out, instu_in[4]);
  and and_1 (R, instu_in[0], instu_in[1], not_1_out, not_2_out, instu_in[4], instu_in[5], not_3_out);
  and and_2 (I_t, instu_in[0], instu_in[1], not_4_out, not_5_out, instu_in[4], not_6_out, not_7_out);
  and and_3 (memread, instu_in[0], instu_in[1], not_8_out, not_9_out, not_10_out, not_11_out, not_12_out);
  and and_4 (memwrite, instu_in[0], instu_in[1], not_13_out, not_14_out, not_15_out, instu_in[5], not_16_out);
  and and_5 (aluop[0], instu_in[0], instu_in[1], not_17_out, not_18_out, not_19_out, instu_in[5], instu_in[6]);
  and and_6 (jal_t, instu_in[0], instu_in[1], instu_in[2], instu_in[3], not_20_out, instu_in[5], instu_in[6]);
  and and_7 (jalr_t, instu_in[0], instu_in[1], instu_in[2], not_21_out, not_22_out, instu_in[5], instu_in[6]);
  or or_1 (regwrite, R, I_t, memread, jal_t, jalr_t);
  or or_2 (alusrc, I_t, memread, memwrite, jalr_t);
  or or_3 (resultsrc[1], jal_t, jalr_t);
  or or_4 (immsrc[0], memwrite, jal_t);
  or or_5 (immsrc[1], aluop[0], jal_t);
  or or_6 (pcsrc[0], take, jalr_t);
  or or_7 (pcsrc[1], jal_t, jalr_t);
  or or_8 (aluop[1], R, I_t);
  or or_9 (lor, memread, memwrite);

  assign branch = aluop[0];
  assign resultsrc[0] = memread;

  // Other names for the same wires on the sheet: branch_t = aluop[0]; ALUsrc_t = alusrc; inst_t[31:0] = instu_in;
  //   o0 = instu_in[0]; op_t[6:0] = instu_in[6:0]; o1 = instu_in[1]; o2 = instu_in[2]; o3 = instu_in[3];
  //   o4 = instu_in[4]; o5 = instu_in[5]; o6 = instu_in[6]; fuct3_t[2:0] = instu_in[14:12];
  //   fuct7_t[6:0] = instu_in[31:25]; R_t = R; regwrite_t = regwrite; load_t = memread; resultsrc0 = memread;
  //   store_t = memwrite
endmodule

module branch (
  input  zero,
  input  lt,
  input  ltu,
  input  [31:0] instu_in,
  input  branch,
  output take
);

  wire beq, beq_t, bge, bge_t, bgeu, bgeu_t, blt, blt_t, bltu, bltu_t, bne, bne_t, not_1_out, not_2_out,
       not_3_out, not_4_out, not_5_out, not_6_out, not_7_out, not_8_out, not_9_out, not_10_out, not_11_out,
       not_12_out, or_1_out;

  not not_1 (not_1_out, instu_in[12]);
  not not_2 (not_2_out, instu_in[13]);
  not not_3 (not_3_out, instu_in[14]);
  not not_4 (not_4_out, instu_in[13]);
  not not_5 (not_5_out, instu_in[14]);
  not not_6 (not_6_out, instu_in[12]);
  not not_7 (not_7_out, instu_in[13]);
  not not_8 (not_8_out, instu_in[13]);
  not not_9 (not_9_out, instu_in[12]);
  not not_10 (not_10_out, zero);
  and and_1 (beq, not_1_out, not_2_out, not_3_out);
  and and_2 (bne, instu_in[12], not_4_out, not_5_out);
  and and_3 (blt, not_6_out, not_7_out, instu_in[14]);
  and and_4 (bge, instu_in[12], not_8_out, instu_in[14]);
  and and_5 (bltu, not_9_out, instu_in[13], instu_in[14]);
  and and_6 (bgeu, instu_in[12], instu_in[13], instu_in[14]);
  and and_7 (beq_t, beq, zero);
  and and_8 (bne_t, bne, not_10_out);
  and and_9 (blt_t, blt, lt);
  not not_11 (not_11_out, lt);
  not not_12 (not_12_out, ltu);
  and and_10 (bge_t, bge, not_11_out);
  and and_11 (bltu_t, bltu, ltu);
  and and_12 (bgeu_t, bgeu, not_12_out);
  or or_1 (or_1_out, beq_t, bne_t, blt_t, bge_t, bltu_t, bgeu_t);
  and and_13 (take, or_1_out, branch);

  // Other names for the same wires on the sheet: branch_t = branch; inst_t[31:0] = instu_in;
  //   op_t[6:0] = instu_in[6:0]; f0 = instu_in[12]; fuct3_t[2:0] = instu_in[14:12]; f1 = instu_in[13];
  //   f2 = instu_in[14]; fuct7_t[6:0] = instu_in[31:25]; lt_t = lt; ltu_t = ltu; zero_t = zero
endmodule

module ALU_decode (
  input  [31:0] instu_in,
  input  [1:0] aluop,
  input  R,
  input  lor,
  output [3:0] sel
);

  wire alu3, branch_sub, f75, not_1_out, not_2_out, not_3_out, not_4_out, not_5_out, not_6_out, not_7_out,
       r_sub, S_R_A;

  and and_1 (f75, instu_in[30], R);
  not not_1 (not_1_out, aluop[1]);
  not not_2 (not_2_out, instu_in[12]);
  not not_3 (not_3_out, instu_in[13]);
  not not_4 (not_4_out, instu_in[14]);
  not not_5 (not_5_out, aluop[0]);
  not not_6 (not_6_out, instu_in[13]);
  not not_7 (not_7_out, aluop[0]);
  and and_2 (branch_sub, aluop[0], not_1_out);
  and and_3 (r_sub, not_2_out, not_3_out, not_4_out, f75, aluop[1], not_5_out);
  and and_4 (S_R_A, instu_in[12], not_6_out, instu_in[14], aluop[1], not_7_out, f75);
  or or_1 (alu3, branch_sub, r_sub, S_R_A);
  Multiplexer #(.width(4)) multiplexer_1 (.in0({alu3, instu_in[14:12]}), .in1(4'b0000), .out(sel), .sel(lor));

  // Other names for the same wires on the sheet: alu_sel[3:0] = {alu3, instu_in[14:12]}; f30 = instu_in[12];
  //   fuct3_t[2:0] = instu_in[14:12]; inst_t[31:0] = instu_in; f31 = instu_in[13]; f32 = instu_in[14];
  //   alu0 = aluop[0]; alu1 = aluop[1]; op_t[6:0] = instu_in[6:0]; fuct7_t[6:0] = instu_in[31:25];
  //   f75_t = instu_in[30]; lor_t = lor; R_t = R
endmodule

module connected (
  input  clk,
  input  reset,
  input  [31:0] in_add,
  input  [31:0] y_input,
  input  first_en_this,
  input  sec_en_this,
  output [31:0] instruction,
  output [31:0] pc_now,
  output [31:0] out_28,
  output [31:0] out_29,
  output [31:0] out_30,
  output [31:0] out_31
);

  wire alusrc, branch_t, lor_t, lt, ltu, memread, memwrite, R_t, take, we, zero;
  wire [1:0] aluop, immscr, pcsrc, resultsrc;
  wire [3:0] sel;
  wire [31:0] dataB, dataD, imm, memout, pcplus4, result, rs1_data, rs2_data;

  pc pc_1 (.pcsrc(pcsrc), .clk(clk), .reset(reset), .imm(imm), .rs1_data(rs1_data), .pc_out(pc_now), .pcplus4(pcplus4));
  ALU alu_1 (.dataA(rs1_data), .dataB(dataB), .sel(sel), .lt(lt), .ltu(ltu), .zero(zero), .dataD(dataD));
  instrmem instrmem_1 (.pc_in(pc_now), .instruction_out(instruction));
  Multiplexer #(.width(32)) multiplexer_1 (.in0(rs2_data), .in1(imm), .out(dataB), .sel(alusrc));
  data_memory data_memory_1 (
    .ALUin(dataD), .in_add(in_add), .memwrite(memwrite), .memread(memread), .clk(clk), .regfilein(rs2_data),
    .inputIn(y_input), .inenable(first_en_this), .inmem(sec_en_this), .memout(memout));
  branch branch_1 (.zero(zero), .lt(lt), .ltu(ltu), .instu_in(instruction), .branch(branch_t), .take(take));
  controlunit controlunit_1 (
    .take(take), .instu_in(instruction), .pcsrc(pcsrc), .resultsrc(resultsrc), .memwrite(memwrite),
    .memread(memread), .alusrc(alusrc), .immsrc(immscr), .regwrite(we), .aluop(aluop), .branch(branch_t),
    .R(R_t), .lor(lor_t));
  ALU_decode alu_decode_1 (.instu_in(instruction), .aluop(aluop), .R(R_t), .lor(lor_t), .sel(sel));
  RegFile regfile_1 (
    .instru_in(instruction), .rd(result), .we(we), .clk(clk), .reset(reset), .rs1(rs1_data), .rs2(rs2_data),
    .out_28(out_28), .out_29(out_29), .Out_30(out_30), .Out_31(out_31));
  immgen immgen_1 (.imm_sel(immscr), .instr(instruction), .imm_out(imm));
  Multiplexer #(.select(2), .width(32)) multiplexer_2 (
    .in0(dataD), .in1(memout), .in2(pcplus4), .out(result), .sel(resultsrc));  // open: in3

  // Other names for the same wires on the sheet: inst_t[31:0] = instruction; reset_t = reset
endmodule

module data_memory (
  input  [31:0] ALUin,
  input  [31:0] in_add,
  input  memwrite,
  input  memread,
  input  clk,
  input  [31:0] regfilein,
  input  [31:0] inputIn,
  input  inenable,
  input  inmem,
  output [31:0] memout
);

  wire and_1_out, not_1_out, or_1_out, or_2_out, or_3_out;
  wire [31:0] multiplexer_1_out, multiplexer_2_out;

  not not_1 (not_1_out, inmem);
  and and_1 (and_1_out, not_1_out, inenable);
  or or_1 (or_1_out, memwrite, inmem);
  or or_2 (or_2_out, clk, and_1_out);
  Multiplexer #(.width(32)) multiplexer_1 (.in0(regfilein), .in1(inputIn), .out(multiplexer_1_out), .sel(inenable));
  or or_3 (or_3_out, memread, inmem);
  Multiplexer #(.width(32)) multiplexer_2 (.in0(ALUin), .in1(in_add), .out(multiplexer_2_out), .sel(inenable));
  RAM #(.dataWidth(32), .trigger("falling")) ram_1 (
    .addr(multiplexer_2_out[9:2]), .we(or_1_out), .oe(or_3_out), .clk(or_2_out), .din(multiplexer_1_out),
    .dout(memout));

  // Other names for the same wires on the sheet: inen = inenable
endmodule
